# Fritzing sketch Circuit Layout (saved by Fritzing 0.9.1b)
breadboards: 7

parts:
  Part2 = Arduino Uno (Rev3)
  J1 = Basic Servo  # not connected
  Part3 = 9 Degrees of Freedom - Sensor Stick
  Part1 = Arduino Mega 2560 (Rev3)
  Raspberry_Pi1 = Raspberry Pi B+  # not connected
  J2 = Basic Servo  # not connected
  J3 = Basic Servo  # not connected
  J5 = Basic Servo  # not connected
  J6 = Basic Servo  # not connected
  J7 = Basic Servo  # not connected
  J8 = Basic Servo  # not connected
  J9 = Basic Servo  # not connected
  J10 = Basic Servo  # not connected
  J11 = Basic Servo  # not connected
  J12 = Basic Servo  # not connected
  J13 = Basic Servo  # not connected
  J14 = Basic Servo  # not connected
  J15 = Basic Servo  # not connected
  J16 = Basic Servo  # not connected
  J17 = Basic Servo  # not connected
  J18 = Basic Servo  # not connected
  J19 = Basic Servo  # not connected
  J20 = Basic Servo  # not connected
  J21 = Basic Servo  # not connected
  J22 = Basic Servo  # not connected
  J23 = Basic Servo  # not connected
  J24 = Basic Servo  # not connected
  J25 = Basic Servo  # not connected
  Part4 = Arduino Uno (Rev3)  # not connected
  VCC1 = 4 x AAA Battery Mount
  U1 = SPM0204UD5 [package=spm0204ud5]  # not connected
  LED1 = LED - 5mm [color="Red (633nm)" package="5 mm [THT]"]
  LED2 = LED - 5mm [color="Red (633nm)" package="5 mm [THT]"]
  R1 = Resistor [tolerance=±5% resistance=220 package=THT]
  R2 = Resistor [tolerance=±5% resistance=220 package=THT]

nets:
  N1: Part2.A4/SDA, Part3.SDA
  N2: Part2.A5/SCL, Part3.SCL
  3V3: Part2.3V3, Part3.VCC
  GND: Part2.GND, Part3.GND
  N3: Part1.GND, VCC1.-
  N4: LED1.anode, R2.Pin_1
  N5: LED2.anode, R1.Pin_1

notes:
  Wires to cover the IMU-9 for stabilization
  Note: this IC is *close* to the IMU09c, but not exact
  Arduino Dedicatd to AHRS calculations
  Leg 1
  Leg 3
  Leg 5
  Leg 7
  Leg 4
  Leg 6
  Leg 2
  Leg 8
  Servo Board 1
  Servo Board 2
  Servo Board 3
  s Servo Board 4
  Note: Do not connect pin 12/13 - used for PWM clocks when using >12 servos
  Our sensor [the ping)))] only has 3 ports (GND, V, SIG)
  HEAD
